# Fritzing sketch Rakathon (saved by Fritzing 0.9.3b)
breadboards: 1

parts:
  Part1 = Arduino Uno (Rev3)
  LCD1 = LCD screen
  R1 = Basic Flex Resistor
  Part2 = InvenSense MPU6050
  RHT1 = Humidity and Temperature Sensor RHT03
  Part3 = Bluetooth HC-05 Macho
  GY-NEO6MV4 = SUP500F [package=sup500f]
  R2 = Trimmer Potentiometer [maximum_resistance=10kΩ package=THT]
  R3 = Resistor [tolerance=±5% resistance=220 package="0603 [SMD]"]
  R4 = Resistor [tolerance=±5% resistance=220 package="2010 [SMD]"]

nets:
  N1: Part1.A0, R4.Pin_0
  N2: Part1.A4/SDA, Part2.SDA
  N3: Part1.A5/SCL, Part2.SCL
  N4: Part1.D8, RHT1.Data-signal
  N5: Part1.D11_PWM/MOSI, LCD1.E
  N6: Part1.D12/MISO, LCD1.RS
  GND: Part1.GND, LCD1.VSS, LCD1.R/W, LCD1.LED-, Part2.GND, RHT1.GND_2, Part3.GND, GY-NEO6MV4.GND, R2.leg1
  N7: Part1.D0/RX, Part3.TXD
  N8: Part1.D1/TX, Part3.RXD
  N9: Part1.D2, LCD1.DB7, Part2.INT
  N10: Part1.D3_PWM, LCD1.DB6, GY-NEO6MV4.RX-I
  N11: Part1.D4, LCD1.DB5, GY-NEO6MV4.TX-O
  N12: Part1.D5_PWM, LCD1.DB4
  3V3: Part1.3V3, RHT1.Vcc
  VCC: Part1.5V, LCD1.VDD, R1.Pin_2, Part2.VCC, Part3.VCC, GY-NEO6MV4.VCC, R2.leg2, R3.Pin_0
  N13: LCD1.V0, R2.wiper
  N14: LCD1.LED+, R3.Pin_1
  N15: R1.pin_1, R4.Pin_1
